// Logisim project main.circ as structural Verilog: 4 circuits, main circuit main
// op
module main (
  input  in_1,
  input  in_2,
  input  in_3,
  input  in_4,
  input  in_5,
  input  in_6,
  input  in_7,
  input  in_8,
  input  in_9,
  input  in_10,
  input  in_11,
  input  in_12,
  input  in_13,
  input  in_14,
  input  in_15,
  input  in_16,
  input  in_17,
  input  in_18,
  input  in_19,
  input  in_20,
  input  in_21
);

  wire _0, _4, _5, _6, _12, _13, _16, clock_1_out, clock_3_out, mipsprogramrom_1_p4, mipsprogramrom_1_p5,
       not_1_out;
  wire [3:0] _7;
  wire [4:0] mipsprogramrom_1_p6, multiplexer_4_out;
  wire [10:6] _14;
  wire [31:0] _1, _3, _11, _15, a, adder_1_out, b, bit_extender_1_out, bit_extender_2_out, mips_alu_3_p4,
       mipsprogramrom_1_p3, multiplexer_1_out, multiplexer_2_out, pc, shifter_1_out;
  wire [31:26] op;

  Adder #(.width(32)) adder_1 (.a(32'h4), .b(pc), .out(adder_1_out));  // open: cin, cout
  Multiplexer #(.select(2), .width(32), .enable("false")) multiplexer_1 (
    .in0(adder_1_out), .in1(_15), .in2(a), .out(multiplexer_1_out), .sel({_16, _13}));  // open: in3
  Register #(.width(32)) register_1 (.D(multiplexer_1_out), .Q(pc), .clk(clock_1_out));  // open: en, clr
  Clock clock_1 (.out(clock_1_out));
  main_controll main_controll_1 (
    .o1(op[31]), .o2(op[30]), .o3(op[29]), .lw(_5), .o4(op[28]), .o5(op[27]), .o6(op[26]), .sw(_4),
    .bne(_12), .Rw(_6), .R(_0));  // open: beq
  jr_control jr_control_1 (.f1(in_16), .f2(in_17), .f3(in_18), .f4(in_19), .f5(in_20), .f6(in_21), .s(_16));
  // MIPSProgramROM mipsprogramrom_1: pin names not known; wires that end beside it: pc, {op, in_6, in_7, in_8, in_9, in_10, in_1, in_2, in_3, in_4, in_5, in_11, in_12, in_13, in_14, in_15, _14, in_16, in_17, in_18, in_19, in_20, in_21}, mipsprogramrom_1_p3, mipsprogramrom_1_p4, mipsprogramrom_1_p5, mipsprogramrom_1_p6
  Multiplexer #(.width(32), .enable("false")) multiplexer_2 (.in0(b), .in1(a), .out(multiplexer_2_out), .sel(_5));
  Multiplexer #(.width(32), .enable("false")) multiplexer_3 (.in0(_1), .in1(_3), .out(mipsprogramrom_1_p3), .sel(_5));
  Clock clock_2 (.out(mipsprogramrom_1_p4));
  and and_1 (mipsprogramrom_1_p5, _6, not_1_out);
  not not_1 (not_1_out, _16);
  assign bit_extender_1_out = {{16{1'b0}}, {in_11, in_12, in_13, in_14, in_15, _14, in_16, in_17, in_18, in_19, in_20, in_21}};  // Bit_Extender bit_extender_1
  Multiplexer #(.width(5), .enable("false")) multiplexer_4 (
    .in0({in_6, in_7, in_8, in_9, in_10}), .in1({in_1, in_2, in_3, in_4, in_5}), .out(multiplexer_4_out),
    .sel(_4));
  Multiplexer #(.select(2), .width(5), .enable("false")) multiplexer_5 (
    .in0({in_1, in_2, in_3, in_4, in_5}), .in1({in_11, in_12, in_13, in_14, in_15}),
    .in2({in_6, in_7, in_8, in_9, in_10}), .out(mipsprogramrom_1_p6), .sel({_4, _0}));  // open: in3
  // Mips_ALU mips_alu_1: pin names not known; wires that end beside it: multiplexer_2_out, bit_extender_1_out, 4'b0010, _11
  // RegisterFile registerfile_1: pin names not known; wires that end beside it: multiplexer_4_out, {in_1, in_2, in_3, in_4, in_5}, a, b
  // Mips_ALU mips_alu_2: pin names not known; wires that end beside it: a, b, _7, _1
  alu_control alu_control_1 (
    .f1(in_16), .f2(in_17), .f3(in_18), .f4(in_19), .f5(in_20), .f6(in_21), .o1(_7[3]), .o2(_7[2]),
    .o3(_7[1]), .o4(_7[0]));
  assign bit_extender_2_out = {{16{in_11}}, {in_11, in_12, in_13, in_14, in_15, _14, in_16, in_17, in_18, in_19, in_20, in_21}};  // Bit_Extender bit_extender_2
  Clock clock_3 (.out(clock_3_out));
  // Mips_ALU mips_alu_3: pin names not known; wires that end beside it: a, b, 4'b1011, mips_alu_3_p4
  Adder #(.width(32)) adder_2 (.a(pc), .b(shifter_1_out), .out(_15));  // open: cin, cout
  Shifter #(.width(32)) shifter_1 (.in(bit_extender_2_out), .\dist (5'b00010), .out(shifter_1_out));
  RAM #(.addrWidth(24), .dataWidth(32), .bus("separate")) ram_1 (
    .addr(_11[23:0]), .din(a), .data(_3), .str(_4), .clk(clock_3_out), .ld(_5));  // open: sel, clr
  and and_2 (_13, _12, mips_alu_3_p4[0]);

  // Other names for the same wires on the sheet: _2[5:0] = {in_16, in_17, in_18, in_19, in_20, in_21};
  //   _14 (some bits) = {in_11, in_12, in_13, in_14, in_15, in_16, in_17, in_18, in_19, in_20, in_21};
  //   op[25:0] = {in_6, in_7, in_8, in_9, in_10, in_1, in_2, in_3, in_4, in_5, in_11, in_12, in_13, in_14, in_15, _14, in_16, in_17, in_18, in_19, in_20, in_21};
  //   _10[4:0] = {in_11, in_12, in_13, in_14, in_15}; _9[4:0] = {in_1, in_2, in_3, in_4, in_5};
  //   _8[4:0] = {in_6, in_7, in_8, in_9, in_10}
endmodule

module alu_control (
  input  f1,
  input  f2,
  input  f3,
  input  f4,
  input  f5,
  input  f6,
  output o1,
  output o2,
  output o3,
  output o4
);


  assign o1 = f4;
  assign o2 = f5;
  assign o3 = f6;
  assign o4 = 1'b0;
endmodule

module main_controll (
  input  o1,
  input  o2,
  input  o3,
  input  o4,
  input  o5,
  input  o6,
  output lw,
  output sw,
  output beq,
  output bne,
  output Rw,
  output R
);

  wire and_1_out, and_2_out, and_3_out, and_4_out, and_5_out, and_6_out, and_7_out, and_8_out, and_9_out,
       and_11_out, and_12_out, not_1_out, not_2_out, not_3_out, not_4_out, not_5_out, not_6_out, not_7_out,
       not_8_out, not_9_out, not_10_out, not_11_out, not_12_out, not_13_out, not_14_out, not_15_out,
       not_16_out, not_17_out, not_18_out, not_19_out, not_20_out, not_21_out, not_22_out, not_23_out,
       not_24_out, not_25_out, not_26_out, not_27_out, not_28_out, not_29_out;

  not not_1 (not_1_out, o3);
  not not_2 (not_2_out, o4);
  not not_3 (not_3_out, o3);
  not not_4 (not_4_out, o4);
  not not_5 (not_5_out, o3);
  not not_6 (not_6_out, o4);
  not not_7 (not_7_out, o3);
  not not_8 (not_8_out, o4);
  not not_9 (not_9_out, o6);
  not not_10 (not_10_out, o6);
  not not_11 (not_11_out, o6);
  not not_12 (not_12_out, o6);
  not not_13 (not_13_out, o6);
  not not_14 (not_14_out, o5);
  not not_15 (not_15_out, o1);
  not not_16 (not_16_out, o2);
  not not_17 (not_17_out, o3);
  not not_18 (not_18_out, o4);
  not not_19 (not_19_out, o5);
  not not_20 (not_20_out, o6);
  not not_21 (not_21_out, o2);
  not not_22 (not_22_out, o3);
  not not_23 (not_23_out, o4);
  not not_24 (not_24_out, o1);
  not not_25 (not_25_out, o2);
  not not_26 (not_26_out, o3);
  not not_27 (not_27_out, o4);
  not not_28 (not_28_out, o5);
  not not_29 (not_29_out, o6);
  and and_1 (and_1_out, not_1_out, not_2_out, o6);
  and and_2 (and_2_out, not_3_out, not_4_out, o5);
  and and_3 (and_3_out, o2, not_5_out, not_6_out);
  and and_4 (and_4_out, o1, not_7_out, not_8_out);
  and and_5 (and_5_out, o5, not_9_out);
  and and_6 (and_6_out, o4, not_10_out);
  and and_7 (and_7_out, o3, not_11_out);
  and and_8 (and_8_out, o2, not_12_out);
  and and_9 (and_9_out, o1, not_13_out);
  and and_10 (bne, not_14_out, o6);
  and and_11 (and_11_out, not_15_out, not_16_out, not_17_out, not_18_out, not_19_out, not_20_out);
  and and_12 (and_12_out, o1, not_21_out, not_22_out, not_23_out, o5, o6);
  and and_13 (R, not_24_out, not_25_out, not_26_out, not_27_out, not_28_out, not_29_out);
  or or_1 (lw, and_1_out, and_2_out, and_3_out, and_4_out);
  or or_2 (beq, and_5_out, and_6_out, and_7_out, and_8_out, and_9_out);
  or or_3 (Rw, and_11_out, and_12_out);

  assign sw = o3;
endmodule

module jr_control (
  input  f1,
  input  f2,
  input  f3,
  input  f4,
  input  f5,
  input  f6,
  output s
);

  wire not_1_out, or_1_out;

  not not_1 (not_1_out, f3);
  or or_1 (or_1_out, not_1_out, f6, f5, f4, f2, f1);
  not not_2 (s, or_1_out);
endmodule
